// Digital circuit  Simulation 03 - 01.dig as structural Verilog
module Simulation_03___01 (
  input  [3:0] In,
  output A,
  output B,
  output C,
  output D,
  output E,
  output F,
  output G
);

  wire _1, _2, _3, _4, _5, _6, _7, _8, _9, not_1_out, not_2_out, not_3_out, not_4_out;

  not not_1 (not_1_out, In[3]);
  not not_2 (not_2_out, In[2]);
  not not_3 (not_3_out, In[1]);
  not not_4 (not_4_out, In[0]);
  and and_1 (_1, not_1_out, In[1], In[0]);
  and and_2 (_2, not_1_out, In[1], not_4_out);
  and and_3 (_3, not_2_out, not_3_out);
  and and_4 (_4, not_1_out, In[2], not_3_out, not_4_out);
  and and_5 (_5, not_1_out, In[2], In[1]);
  and and_6 (_6, not_2_out, not_3_out, not_4_out);
  and and_7 (_7, In[3], not_2_out, not_3_out);
  and and_8 (_8, not_1_out, In[2], not_3_out, In[0]);
  and and_9 (_9, not_1_out, not_2_out, In[1]);
  or or_1 (A, _5, _6, _7, _8, _9);
  or or_2 (B, _1, _3, _4, _9);
  or or_3 (C, _1, _3, _4, _5, _8);
  or or_4 (D, _2, _6, _7, _8, _9);
  or or_5 (E, _2, _6);
  or or_6 (F, _4, _5, _6, _7, _8);
  or or_7 (G, _2, _4, _7, _8, _9);
  Seven_Seg seven_seg_1 (.a(A), .b(B), .c(C), .d(D), .e(E), .f(F), .g(G), .dp(1'b0));
endmodule
