// Digital circuit backup_1.dig as structural Verilog
module backup_1 (
  input  [8:0] N,
  input  reset,
  input  start,
  input  clock,
  input  [1:0] in_9,
  input  in_10,
  input  clk,
  input  [2:0] in_13,
  input  [1:0] in_15,
  input  r_w,
  input  off_on,
  output done,
  output [7:0] displayout,
  output [15:0] clockcount,
  output valid,
  output [1:0] out_11,
  output [1:0] out_14,
  output [8:0] addr,
  output [7:0] val,
  output [7:0] rom_addr,
  output [8:0] tmp_val,
  output [8:0] n_2,
  output [8:0] out_23,
  output [7:0] out_24
);

  wire _000, _001, _010, _011, _100, _101, _110, addr_lt_n, addr_lt_n_1, and_1_out, and_2_out, and_3_out,
       and_4_out, and_5_out, and_6_out, and_7_out, and_8_out, and_9_out, d_ff_1_nq, d_ff_6_q, d_ff_7_q,
       or_1_out, or_2_out, or_3_out, or_5_out, or_6_out, or_7_out, or_8_out, or_9_out, or_10_out, Q0, Q1, Q2,
       start_t, tmp_val__gt_0;
  wire [1:1] or_4_out;
  wire [7:0] add_1_s;
  wire [8:0] add_2_s, multiplexer_1_out, multiplexer_3_out, multiplexer_4_out, n_1, tmp_val__1,
       tmp_val__plus_1;

  and and_1 (and_1_out, _000, start_t);
  and and_2 (and_2_out, _010, ~addr_lt_n_1);  // And
  and and_3 (and_3_out, _100, ~addr_lt_n);  // And
  and and_4 (and_4_out, _100, addr_lt_n, tmp_val__gt_0);
  and and_5 (and_5_out, _100, addr_lt_n, ~tmp_val__gt_0);  // And
  and and_6 (and_6_out, _100, ~addr_lt_n);  // And
  or or_1 (or_1_out, and_1_out, and_2_out, and_3_out, and_4_out, done);
  or or_2 (or_2_out, _001, _010, done, and_5_out, and_6_out);
  or or_3 (or_3_out, _011, _100, done, _101, _110);
  and and_7 (and_7_out, or_1_out, ~reset);  // And
  and and_8 (and_8_out, or_2_out, ~reset);  // And
  and and_9 (and_9_out, or_3_out, ~reset);  // And
  D_FF d_ff_1 (.D(start), .C(clock), .nQ(d_ff_1_nq));  // open: Q
  D_FF d_ff_2 (.D(and_7_out), .C(clock), .Q(Q0));  // open: nQ
  D_FF d_ff_3 (.D(and_8_out), .C(clock), .Q(Q1));  // open: nQ
  D_FF d_ff_4 (.D(and_9_out), .C(clock), .Q(Q2));  // open: nQ
  Multiplexer #(.Bits(9)) multiplexer_1 (.sel(_000), .in_0(out_23), .in_1(N), .out(multiplexer_1_out));
  D_FF #(.Bits(9)) d_ff_5 (.D(multiplexer_1_out), .C(clock), .Q(out_23));  // open: nQ
  D_FF d_ff_6 (.D(start), .C(clock), .Q(d_ff_6_q));  // open: nQ
  D_FF d_ff_7 (.D(d_ff_1_nq), .C(clock), .Q(d_ff_7_q));  // open: nQ
  and and_10 (start_t, d_ff_6_q, d_ff_7_q);
  Add #(.Bits(8)) add_1 (.a(displayout), .b(8'h1), .c_i(1'b0), .s(add_1_s));  // open: c_o
  or or_4 (or_4_out[1], _001, _010);
  or or_5 (or_5_out, _000, _101, _100, _110);
  Add #(.Bits(9)) add_2 (.a(addr), .b(9'h1), .c_i(1'b0), .s(add_2_s));  // open: c_o
  or or_6 (or_6_out, _010, _101);
  or or_7 (or_7_out, _000, _010, _011, _101);
  Add #(.Bits(9)) add_3 (.a(tmp_val), .b(9'h1), .c_i(1'b0), .s(tmp_val__plus_1));  // open: c_o
  Sub #(.Bits(9)) sub_1 (.a(tmp_val), .b(9'h1), .c_i(1'b0), .s(tmp_val__1));  // open: c_o
  Comparator #(.Bits(9)) comparator_1 (.a(tmp_val), .b({9{1'b0}}), .gt(tmp_val__gt_0));  // open: eq, lt
  Multiplexer #(.Selector_Bits(2), .Bits(8)) multiplexer_2 (
    .sel({or_4_out[1], _110}), .in_0({8{1'b0}}), .in_1(add_1_s), .in_2(rom_addr), .in_3(8'h45), .out(out_24));
  or or_8 (or_8_out, _001, _010, _011, _110);
  Register register_1 (.D(_101), .C(clock), .en(or_5_out), .Q(valid));
  Multiplexer #(.Bits(9)) multiplexer_3 (.sel(or_6_out), .in_0({9{1'b0}}), .in_1(add_2_s), .out(multiplexer_3_out));
  Register #(.Bits(8)) register_2 (.D(out_24), .C(clock), .en(or_8_out), .Q(displayout));
  Sub #(.Bits(9)) sub_2 (.a(n_2), .b(9'h1), .c_i(1'b0), .s(n_1));  // open: c_o
  Comparator #(.Bits(9)) comparator_2 (.a(addr), .b(n_1), .lt(addr_lt_n_1));  // open: gt, eq
  Comparator #(.Bits(9)) comparator_3 (.a(addr), .b(n_2), .lt(addr_lt_n));  // open: gt, eq
  Register #(.Bits(9)) register_3 (.D(out_23), .C(clock), .en(_000), .Q(n_2));
  Register #(.Bits(9)) register_4 (.D(multiplexer_3_out), .C(clock), .en(or_7_out), .Q(addr));
  or or_9 (or_9_out, _010, _101);
  or or_10 (or_10_out, _010, _100, _101);
  Multiplexer #(.Bits(9)) multiplexer_4 (
    .sel(_101), .in_0(tmp_val__plus_1), .in_1(tmp_val__1), .out(multiplexer_4_out));
  ROM #(.AddrBits(9), .Bits(8)) ROMFILE (.A(addr), .sel(1'b1), .D(rom_addr));
  RAMDualPort #(.AddrBits(9), .Bits(8)) RAM (.A(addr), .Din(displayout), .str(_101), .C(clock), .ld(_101));  // open: D
  Decoder #(.Selector_Bits(3)) decoder_1 (
    .sel({Q2, Q1, Q0}), .out_0(_000), .out_1(_001), .out_2(_010), .out_3(_011), .out_4(_100), .out_5(_101),
    .out_6(_110), .out_7(done));
  RAMDualPort #(.AddrBits(8), .Bits(9)) tmp (
    .A(displayout), .Din(multiplexer_4_out), .str(or_9_out), .C(clock), .ld(or_10_out), .D(tmp_val));
  Seven_Seg_Hex seven_seg_hex_1 (.d(displayout[7:4]), .dp(1'b0));
  Seven_Seg_Hex seven_seg_hex_2 (.d(displayout[3:0]), .dp(1'b0));
  ROM #(.Bits(2)) rom_1 (.A(in_9), .sel(in_10), .D(out_11));
  RAMDualPort #(.AddrBits(3), .Bits(2)) RAM_2 (.A(in_13), .Din(in_15), .str(r_w), .C(clk), .ld(off_on), .D(out_14));

  assign clockcount = 16'h1;
  assign val = displayout;

  // Other names for the same wires on the sheet: _111 = done; clk_t = clock; N_t[8:0] = out_23; n_t_t[8:0] = n_2

  // Notes on the sheet:
  //   contents of ROMFILE (hex, n*v repeats v):
  //   1,0,3
  //   contents of rom_1 (hex, n*v repeats v):
  //   0,1,2,3
endmodule
