// Digital circuit rom.dig as structural Verilog
module rom (
  input  [1:0] in_1,
  input  in_2,
  input  clk,
  input  [2:0] in_5,
  input  [1:0] in_7,
  input  r_w,
  input  off_on,
  input  [8:0] P5,
  input  clock,
  input  clk_2,
  input  [2:0] in_13,
  input  r_w_2,
  input  off_on_2,
  output [1:0] out_3,
  output [1:0] out_6
);

  wire [1:0] tmp_val, tmp_val__plus_1;

  Add #(.Bits(2)) add_1 (.a(tmp_val), .b(2'b01), .c_i(1'b0), .s(tmp_val__plus_1));  // open: c_o
  ROM #(.Bits(2)) rom_1 (.A(in_1), .sel(in_2), .D(out_3));
  RAMDualPort #(.AddrBits(3), .Bits(2)) RAM (.A(in_5), .Din(in_7), .str(r_w), .C(clk), .ld(off_on), .D(out_6));
  RAMDualPort #(.AddrBits(3), .Bits(2)) RAM_2 (
    .A(in_13), .Din(tmp_val__plus_1), .str(r_w_2), .C(clk_2), .ld(off_on_2), .D(tmp_val));

  // Other names for the same wires on the sheet: clk_t = clock

  // Notes on the sheet:
  //   contents of rom_1 (hex, n*v repeats v):
  //   0,1,2,3
endmodule
