// Digital circuit 03_Template.dig as structural Verilog
module _03_Template (
  input  A,
  input  B,
  input  Cin,
  output Sum,
  output Cout
);

  wire and_1_out, and_2_out, and_3_out, and_4_out, and_5_out, and_6_out, not_1_out, not_2_out, not_3_out,
       not_4_out, or_1_out;

  not not_1 (not_1_out, A);
  not not_2 (not_2_out, B);
  not not_3 (not_3_out, Cin);
  and and_1 (and_1_out, A, not_2_out);
  and and_2 (and_2_out, not_1_out, B);
  and and_3 (and_3_out, B, A);
  or or_1 (or_1_out, and_1_out, and_2_out);
  not not_4 (not_4_out, or_1_out);
  and and_4 (and_4_out, or_1_out, Cin);
  and and_5 (and_5_out, or_1_out, not_3_out);
  and and_6 (and_6_out, not_4_out, Cin);
  or or_2 (Sum, and_5_out, and_6_out);
  or or_3 (Cout, and_3_out, and_4_out);
endmodule
