// Digital circuit cyclic.dig as structural Verilog
module cyclic (
  input  A,
  input  B,
  input  C,
  input  D,
  output _3,
  output _2,
  output _1,
  output _0
);

  wire and_1_out, and_3_out, and_4_out, and_5_out, and_6_out, and_7_out, not_1_out, not_2_out, not_3_out,
       not_4_out;

  not not_1 (not_1_out, A);
  not not_2 (not_2_out, B);
  not not_3 (not_3_out, C);
  not not_4 (not_4_out, D);
  and and_1 (and_1_out, not_1_out, not_3_out, D);
  and and_2 (_3, A, not_2_out, not_3_out);
  and and_3 (and_3_out, not_1_out, C, not_4_out);
  and and_4 (and_4_out, not_1_out, not_2_out, C);
  and and_5 (and_5_out, not_2_out, not_3_out, D);
  and and_6 (and_6_out, not_1_out, B, not_3_out);
  and and_7 (and_7_out, not_1_out, B);
  or or_1 (_2, _3, and_7_out);
  or or_2 (_1, and_4_out, and_6_out);
  or or_3 (_0, and_1_out, and_3_out, and_5_out);
endmodule
