// Digital circuit hammerA.dig as structural Verilog
module hammerA (
  input  _1,
  input  _2,
  input  _3,
  input  _4,
  input  _5,
  input  _6,
  input  _7,
  output C1,
  output C2,
  output C3
);

  xor xor_1 (C1, _4, _5, _6, _7);
  xor xor_2 (C2, _2, _3, _6, _7);
  xor xor_3 (C3, _1, _3, _5, _7);
endmodule
