// Digital circuit 642-3-code.dig as structural Verilog
module _642_3_code (
  input  A,
  input  B,
  input  C,
  input  D,
  output _3,
  output _2,
  output _1,
  output _0
);

  wire and_1_out, and_2_out, and_3_out, and_4_out, and_5_out, and_6_out, and_7_out, not_1_out, not_2_out,
       not_3_out, not_4_out;

  not not_1 (not_1_out, A);
  not not_2 (not_2_out, B);
  not not_3 (not_3_out, C);
  not not_4 (not_4_out, D);
  and and_1 (and_1_out, not_1_out, B, C);
  and and_2 (and_2_out, A, not_2_out, not_3_out);
  and and_3 (and_3_out, not_1_out, B, not_4_out);
  and and_4 (and_4_out, not_1_out, C, not_4_out);
  and and_5 (and_5_out, not_2_out, not_3_out, D);
  and and_6 (and_6_out, not_1_out, B, not_3_out, D);
  and and_7 (and_7_out, not_1_out, C, D);
  or or_1 (_3, and_2_out, and_6_out, and_7_out);
  or or_2 (_2, and_1_out, and_3_out, and_5_out);
  or or_3 (_1, and_2_out, and_4_out, and_6_out);
  or or_4 (_0, and_5_out, and_6_out, and_7_out);
endmodule
