// Digital circuit Templatet.dig as structural Verilog
module Templatet (
  input  [3:0] In,
  input  [1:0] Selector,
  output [3:0] Output
);

  wire _0c, _0e, _1c, _1e, _02, _2c, _2e, _3c, _3e, _06, _12, _16, _22, _26, _32, _36, and_1_out, and_2_out,
       and_3_out, and_4_out, and_5_out, and_6_out, and_7_out, and_8_out, and_9_out, and_10_out, and_11_out,
       and_12_out, and_13_out, and_14_out, and_15_out, and_16_out, not_1_out, not_2_out;

  not not_1 (not_1_out, Selector[1]);
  not not_2 (not_2_out, Selector[0]);
  and and_1 (and_1_out, not_1_out, not_2_out, _0e);
  and and_2 (and_2_out, not_1_out, Selector[0], _0c);
  and and_3 (and_3_out, Selector[1], not_2_out, _02);
  and and_4 (and_4_out, Selector[1], Selector[0], _06);
  and and_5 (and_5_out, not_1_out, not_2_out, _1e);
  and and_6 (and_6_out, not_1_out, Selector[0], _1c);
  and and_7 (and_7_out, Selector[1], not_2_out, _12);
  and and_8 (and_8_out, Selector[1], Selector[0], _16);
  and and_9 (and_9_out, not_1_out, not_2_out, _2e);
  and and_10 (and_10_out, not_1_out, Selector[0], _2c);
  and and_11 (and_11_out, Selector[1], not_2_out, _22);
  and and_12 (and_12_out, Selector[1], Selector[0], _26);
  and and_13 (and_13_out, not_1_out, not_2_out, _3e);
  and and_14 (and_14_out, not_1_out, Selector[0], _3c);
  and and_15 (and_15_out, Selector[1], not_2_out, _32);
  and and_16 (and_16_out, Selector[1], Selector[0], _36);
  excess_3 excess_3_1 (.A(In[3]), .B(In[2]), .C(In[1]), .D(In[0]), ._3(_3e), ._2(_2e), ._1(_1e), ._0(_0e));
  or or_1 (Output[0], and_1_out, and_2_out, and_3_out, and_4_out);
  or or_2 (Output[1], and_5_out, and_6_out, and_7_out, and_8_out);
  or or_3 (Output[2], and_9_out, and_10_out, and_11_out, and_12_out);
  or or_4 (Output[3], and_13_out, and_14_out, and_15_out, and_16_out);
  cyclic cyclic_1 (.A(In[3]), .B(In[2]), .C(In[1]), .D(In[0]), ._3(_3c), ._2(_2c), ._1(_1c), ._0(_0c));
  _2421_code _2421_code_1 (.A(In[3]), .B(In[2]), .C(In[1]), .D(In[0]), ._3(_32), ._2(_22), ._1(_12), ._0(_02));
  _642_3_code _642_3_code_1 (.A(In[3]), .B(In[2]), .C(In[1]), .D(In[0]), ._3(_36), ._2(_26), ._1(_16), ._0(_06));

  // Other names for the same wires on the sheet: _0ans = Output[0]; _1ans = Output[1]; _2ans = Output[2];
  //   _3ans = Output[3]; D = In[0]; C = In[1]; B = In[2]; A = In[3]
endmodule
