// Digital circuit Template.dig as structural Verilog
module Template (
  input  [6:0] In,
  output _1,
  output _2,
  output _3,
  output _4,
  output _5,
  output _6,
  output _7
);

  wire hammera_1_c1, hammera_1_c2, hammera_1_c3, not_1_out, not_2_out, not_3_out, not_4_out, not_5_out,
       not_6_out, not_7_out;
  wire [6:0] hammerb_1__1;

  not not_1 (not_1_out, In[6]);
  not not_2 (not_2_out, In[5]);
  not not_3 (not_3_out, In[4]);
  not not_4 (not_4_out, In[3]);
  not not_5 (not_5_out, In[2]);
  not not_6 (not_6_out, In[1]);
  not not_7 (not_7_out, In[0]);
  hammerA hammera_1 (
    ._1(In[0]), ._2(In[1]), ._3(In[2]), ._4(In[3]), ._5(In[4]), ._6(In[5]), ._7(In[6]), .C1(hammera_1_c1),
    .C2(hammera_1_c2), .C3(hammera_1_c3));
  hammerB hammerb_1 (
    .C1(hammera_1_c1), .C2(hammera_1_c2), .C3(hammera_1_c3), ._1(hammerb_1__1[0]), ._2(hammerb_1__1[1]),
    ._3(hammerb_1__1[2]), ._4(hammerb_1__1[3]), ._5(hammerb_1__1[4]), ._6(hammerb_1__1[5]),
    ._7(hammerb_1__1[6]));
  hammerC hammerc_1 (.B(hammerb_1__1), .In(In), ._1(_1), ._2(_2), ._3(_3), ._4(_4), ._5(_5), ._6(_6), ._7(_7));
endmodule
