// Digital circuit hammerB.dig as structural Verilog
module hammerB (
  input  C1,
  input  C2,
  input  C3,
  output _1,
  output _2,
  output _3,
  output _4,
  output _5,
  output _6,
  output _7
);

  wire not_1_out, not_2_out, not_3_out;

  not not_1 (not_1_out, C1);
  not not_2 (not_2_out, C2);
  not not_3 (not_3_out, C3);
  and and_1 (_1, not_1_out, not_2_out, C3);
  and and_2 (_2, not_1_out, C2, not_3_out);
  and and_3 (_3, not_1_out, C2, C3);
  and and_4 (_4, C1, not_2_out, not_3_out);
  and and_5 (_5, C1, not_2_out, C3);
  and and_6 (_6, C1, C2, not_3_out);
  and and_7 (_7, C1, C2, C3);
endmodule
