// Digital circuit hammerC.dig as structural Verilog
module hammerC (
  input  [6:0] B,
  input  [6:0] In,
  output _1,
  output _2,
  output _3,
  output _4,
  output _5,
  output _6,
  output _7
);

  assign {_7, _6, _5, _4, _3, _2, _1} = B ^ In;  // XOr xor_1, 7 bits wide
endmodule
