// Digital circuit Template.dig as structural Verilog
module Template (
  input  A,
  input  B,
  input  C,
  input  D,
  output Before,
  output After
);

  wire and_1_out, and_2_out, and_3_out, and_4_out;

  and and_1 (and_1_out, ~C, D);  // And
  and and_2 (and_2_out, ~B, D);  // And
  and and_3 (and_3_out, ~C, D);  // And
  and and_4 (and_4_out, A, ~B, D);  // And
  or or_1 (After, and_1_out, and_2_out, ~A);  // Or
  or or_2 (Before, and_3_out, and_4_out, ~A);  // Or
endmodule

/* Test case test:
A B C D Before After
0 0 0 0 1 1
0 0 0 1 1 1
0 0 1 0 1 1
0 0 1 1 1 1
0 1 0 0 1 1
0 1 0 1 1 1
0 1 1 0 1 1
0 1 1 1 1 1
1 0 0 0 0 0
1 0 0 1 1 1
1 0 1 0 0 0
1 0 1 1 1 1
1 1 0 0 0 0
1 1 0 1 1 1
1 1 1 0 0 0
1 1 1 1 0 0
1 0 0 1 1 1
0 0 0 1 1 1
1 0 1 1 1 1
0 0 1 1 1 1
1 0 1 1 1 1
0 0 1 1 1 1
1 0 1 1 1 1
0 0 1 1 1 1
*/
