// Digital circuit Template.dig as structural Verilog
module Template (
  input  [7:0] In,
  output [8:0] Output,
  output [8:0] out_3,
  output [8:0] out_4
);

  assign out_3 = ~{1'b0, In};  // Not not_1, 9 bits wide
  Add #(.Bits(9)) add_1 (.a(out_3), .b(9'h1), .c_i(1'b0), .s(Output));  // open: c_o

  assign out_4 = 9'h1;
endmodule
