// Digital circuit test.dig as structural Verilog
module test (
  input  A,
  output B
);

  wire not_1_out;

  not not_1 (not_1_out, A);
  and and_1 (B, A, not_1_out);
endmodule

/* Test case test:
A B
0 0
1 0
0 0
1 0
0 0
1 0
*/
