// Digital circuit Template.dig as structural Verilog
module Template (
  input  A,
  input  B,
  input  C,
  input  D,
  input  E,
  input  F,
  output Before,
  output After
);

  wire and_1_out, and_2_out, and_3_out, and_4_out, and_5_out, and_6_out, and_7_out, and_8_out, not_1_out,
       not_2_out, not_3_out, not_4_out, not_5_out, not_6_out, not_7_out, not_8_out, not_9_out;

  not not_1 (not_1_out, A);
  not not_2 (not_2_out, C);
  not not_3 (not_3_out, D);
  not not_4 (not_4_out, E);
  not not_5 (not_5_out, A);
  not not_6 (not_6_out, E);
  not not_7 (not_7_out, F);
  not not_8 (not_8_out, A);
  not not_9 (not_9_out, B);
  and and_1 (and_1_out, ~A, ~C, ~D, ~E);  // And
  and and_2 (and_2_out, ~A, D, ~E, ~F);  // And
  and and_3 (and_3_out, ~A, ~B, E, F);  // And
  and and_4 (and_4_out, ~A, ~C, ~F, ~E);  // And
  and and_5 (and_5_out, ~A, ~C, ~D, ~B, F);  // And
  and and_6 (and_6_out, not_1_out, not_2_out, not_3_out, not_4_out);
  and and_7 (and_7_out, not_5_out, D, not_6_out, not_7_out);
  and and_8 (and_8_out, not_8_out, not_9_out, E, F);
  or or_1 (Before, and_6_out, and_7_out, and_8_out);
  or or_2 (After, and_1_out, and_2_out, and_3_out, and_4_out, and_5_out);
endmodule

/* Test case test:
A B C D E F Before After
0 0 0 0 0 1 1 1
0 0 0 0 1 1 1 1
0 0 0 0 0 1 1 1
0 0 0 0 1 1 1 1
0 0 0 0 0 0 1 1
0 0 0 0 1 0 1 1
0 0 0 0 0 1 1 1
0 0 0 0 1 1 1 1
*/
