// Digital circuit Template.dig as structural Verilog
module Template (
  input  [3:0] In,
  output [3:0] Output,
  output [2:0] out_3,
  output [2:0] out_4
);

  wire [2:0] not_1_out;

  assign not_1_out = ~In[2:0];  // Not not_1, 3 bits wide
  Add #(.Bits(3)) add_1 (.a(not_1_out), .b(3'b001), .c_i(1'b0), .s(out_3));  // open: c_o
  Multiplexer #(.Bits(4)) multiplexer_1 (.sel(In[3]), .in_0(In), .in_1({In[3], out_3}), .out(Output));

  assign out_4 = In[2:0];
endmodule
