// Digital circuit Template.dig as structural Verilog
module Template (
  input  [3:0] A,
  input  [3:0] B,
  input  [2:0] S,
  input  M,
  input  C,
  output [3:0] F,
  output [3:0] out_7
);

  wire [3:0] A_t, add_3_s, add_4_s, add_5_s, add_6_s, add_7_s, add_8_s, add_9_s, add_10_s, add_11_s,
       add_12_s, and_1_out, and_2_out, B_t, C0, C1, multiplexer_4_out, nand_1_out, nor_1_out, not_1_out,
       not_2_out, or_1_out, xnor_1_out;

  Add #(.Bits(4)) add_1 (.a(not_1_out), .b(4'b0001), .c_i(1'b0), .s(A_t));  // open: c_o
  Add #(.Bits(4)) add_2 (.a(not_2_out), .b(4'b0001), .c_i(1'b0), .s(B_t));  // open: c_o
  assign not_1_out = ~A;  // Not not_1, 4 bits wide
  assign not_2_out = ~B;  // Not not_2, 4 bits wide
  assign nand_1_out = ~(A & B);  // NAnd nand_1, 4 bits wide
  assign nor_1_out = ~(A | B);  // NOr nor_1, 4 bits wide
  assign xnor_1_out = ~(A ^ B);  // XNOr xnor_1, 4 bits wide
  assign and_1_out = A & B;  // And and_1, 4 bits wide
  assign or_1_out = A | B;  // Or or_1, 4 bits wide
  assign and_2_out = A & not_2_out;  // And and_2, 4 bits wide
  Add #(.Bits(4)) add_3 (.a(A), .b(B_t), .c_i(1'b0), .s(add_3_s));  // open: c_o
  Add #(.Bits(4)) add_4 (.a(A), .b(B), .c_i(1'b0), .s(add_4_s));  // open: c_o
  Add #(.Bits(4)) add_5 (.a(A), .b(B_t), .c_i(1'b0), .s(add_5_s));  // open: c_o
  Add #(.Bits(4)) add_6 (.a(B), .b(4'b0001), .c_i(1'b0), .s(add_6_s));  // open: c_o
  Add #(.Bits(4)) add_7 (.a(A), .b(4'b1111), .c_i(1'b0), .s(add_7_s));  // open: c_o
  Add #(.Bits(4)) add_8 (.a(A), .b(B), .c_i(1'b0), .s(add_8_s));  // open: c_o
  Add #(.Bits(4)) add_9 (.a(add_3_s), .b(4'b1111), .c_i(1'b0), .s(add_9_s));  // open: c_o
  Add #(.Bits(4)) add_10 (.a(A_t), .b(4'b1111), .c_i(1'b0), .s(add_10_s));  // open: c_o
  Add #(.Bits(4)) add_11 (.a(A), .b(4'b0001), .c_i(1'b0), .s(add_11_s));  // open: c_o
  Add #(.Bits(4)) add_12 (.a(add_4_s), .b(4'b0001), .c_i(1'b0), .s(add_12_s));  // open: c_o
  Multiplexer #(.Bits(4), .Selector_Bits(3)) multiplexer_1 (
    .sel(S), .in_0(not_1_out), .in_1(nand_1_out), .in_2(nor_1_out), .in_3(xnor_1_out), .in_4(and_1_out),
    .in_5(or_1_out), .in_6(and_2_out), .in_7(A), .out(out_7));
  Multiplexer #(.Selector_Bits(3), .Bits(4)) multiplexer_2 (
    .sel(S), .in_0(A), .in_1(add_7_s), .in_2(add_8_s), .in_3(add_9_s), .in_4(add_10_s), .in_5(B),
    .in_6({A[2:0], 1'b0}), .in_7({1'b0, A[3:1]}), .out(C0));
  Multiplexer #(.Selector_Bits(3), .Bits(4)) multiplexer_3 (
    .sel(S), .in_0(add_11_s), .in_1(A), .in_2(add_12_s), .in_3(add_5_s), .in_4(A_t), .in_5(add_6_s),
    .in_6(4'b0000), .in_7(4'b0000), .out(C1));
  Multiplexer #(.Bits(4)) multiplexer_4 (.sel(C), .in_0(C0), .in_1(C1), .out(multiplexer_4_out));
  Multiplexer #(.Bits(4)) multiplexer_5 (.sel(M), .in_0(out_7), .in_1(multiplexer_4_out), .out(F));
endmodule
