// Digital circuit Template.dig as structural Verilog
module Template (
  input  A,
  input  B,
  input  Clr,
  input  Clock,
  output Z
);

  wire add_1_c_o, add_1_s, d_ff_as_1_q, not_1_out;

  not not_1 (not_1_out, Clr);
  Add add_1 (.a(A), .b(B), .c_i(d_ff_as_1_q), .s(add_1_s), .c_o(add_1_c_o));
  D_FF_AS d_ff_as_1 (.Set(1'b0), .D(add_1_c_o), .C(Clock), .Clr(not_1_out), .Q(d_ff_as_1_q));  // open: nQ
  and and_1 (Z, add_1_s, Clr);
endmodule
