// Digital circuit 3.1.dig as structural Verilog
module _3_1 (
  input  P,
  input  Clr,
  input  clock,
  output Z
);

  wire and_1_out, d_ff_1_q, not_1_out, not_2_out;

  and and_1 (and_1_out, not_1_out, P);
  not not_1 (not_1_out, Clr);
  D_FF d_ff_1 (.D(and_1_out), .C(clock), .Q(d_ff_1_q));  // open: nQ
  and and_2 (Z, not_2_out, and_1_out);
  not not_2 (not_2_out, d_ff_1_q);
endmodule
