// Digital circuit Template.dig as structural Verilog
module Template (
  input  P,
  input  Clr,
  input  clock,
  output Z,
  output Z_2,
  output Z_3
);

  wire and_1_out, and_4_out, d_ff_1_q, d_ff_2_nq, d_ff_3_nq, d_ff_4_q, d_ff_5_nq, d_ff_6_q, d_ff_7_q,
       d_ff_8_q, d_ff_9_q, not_1_out;

  not not_1 (not_1_out, Clr);
  and and_1 (and_1_out, P, not_1_out);
  D_FF d_ff_1 (.D(and_1_out), .C(clock), .Q(d_ff_1_q));  // open: nQ
  D_FF d_ff_2 (.D(d_ff_1_q), .C(clock), .nQ(d_ff_2_nq));  // open: Q
  D_FF d_ff_3 (.D(d_ff_4_q), .C(clock), .nQ(d_ff_3_nq));  // open: Q
  D_FF d_ff_4 (.D(and_1_out), .C(clock), .Q(d_ff_4_q));  // open: nQ
  D_FF d_ff_5 (.D(and_1_out), .C(clock), .nQ(d_ff_5_nq));  // open: Q
  D_FF d_ff_6 (.D(and_1_out), .C(clock), .Q(d_ff_6_q));  // open: nQ
  D_FF d_ff_7 (.D(d_ff_5_nq), .C(clock), .Q(d_ff_7_q));  // open: nQ
  D_FF d_ff_8 (.D(d_ff_1_q), .C(clock), .Q(d_ff_8_q));  // open: nQ
  D_FF d_ff_9 (.D(d_ff_2_nq), .C(clock), .Q(d_ff_9_q));  // open: nQ
  and and_2 (Z_2, d_ff_6_q, d_ff_7_q);
  and and_3 (Z_3, d_ff_8_q, d_ff_9_q);
  and and_4 (and_4_out, d_ff_3_nq, d_ff_4_q);
  D_FF d_ff_10 (.D(and_4_out), .C(clock), .Q(Z));  // open: nQ
endmodule
