// Digital circuit Template.dig as structural Verilog
module Template (
  input  P,
  input  Clr,
  input  clock,
  output Z
);

  wire and_1_out, d_ff_1_nq, d_ff_2_q, not_1_out;

  not not_1 (not_1_out, Clr);
  and and_1 (and_1_out, not_1_out, P);
  D_FF d_ff_1 (.D(d_ff_2_q), .C(clock), .nQ(d_ff_1_nq));  // open: Q
  D_FF d_ff_2 (.D(and_1_out), .C(clock), .Q(d_ff_2_q));  // open: nQ
  and and_2 (Z, d_ff_1_nq, d_ff_2_q);
endmodule
