// Digital circuit SinglePulser.dig as structural Verilog
module SinglePulser (
  input  Clr,
  input  Clock,
  input  P,
  output Z
);

  wire and_1_out, and_2_out, and_3_out, and_4_out, and_5_out, not_1_out, not_2_out, or_1_out, Z_0_n, Z_1_n;

  not not_1 (not_1_out, Z_1_n);
  not not_2 (not_2_out, Z_0_n);
  and and_1 (and_1_out, P, Z_0_n);
  and and_2 (and_2_out, P, Z_1_n);
  and and_3 (and_3_out, P, not_2_out, not_1_out);
  or or_1 (or_1_out, and_1_out, and_2_out);
  and and_4 (and_4_out, or_1_out, ~Clr);  // And
  and and_5 (and_5_out, and_3_out, ~Clr);  // And
  and and_6 (Z, Z_0_n, ~Clr);  // And
  D_FF u_Z_1_n (.D(and_4_out), .C(Clock), .Q(Z_1_n));  // open: nQ
  D_FF u_Z_0_n (.D(and_5_out), .C(Clock), .Q(Z_0_n));  // open: nQ
  // Probe state on {Z_1_n, Z_0_n}
endmodule
