// Digital circuit Solution.dig as structural Verilog
module Solution (
  input  P5,
  input  reset,
  input  clock,
  input  P10,
  input  P20,
  input  Pcoffee,
  input  Ptea,
  input  Pchange,
  input  Pnext,
  output [5:0] Balance,
  output CoffeeOut,
  output TeaOut,
  output [1:0] Change5,
  output [1:0] Change10,
  output [1:0] Change20
);

  wire c5, c10, c20, cCoffee, cTea, M20, M25, M30, M40, M45, multiplexer_4_out, multiplexer_5_out,
       multiplexer_11_out, multiplexer_12_out, NcoffeeOut, NteaOut, p5_t, p10_t, p20_t, pChange_t, pCoffee_t,
       pNext_t, pReset, ProductOut, pTea_t;
  wire [1:0] lookuptable_1_out, lookuptable_2_out, lookuptable_3_out, Nchange5, Nchange10, Nchange20;
  wire [5:0] A5, A10, A20, ACoffee, ATea, multiplexer_1_out, multiplexer_2_out, multiplexer_3_out,
       multiplexer_7_out, multiplexer_8_out, multiplexer_9_out, multiplexer_10_out, Nbalance;

  Multiplexer #(.Bits(6)) multiplexer_1 (.sel(pChange_t), .in_0(Balance), .in_1({6{1'b0}}), .out(multiplexer_1_out));
  SinglePulser singlepulser_1 (.Clr(reset), .Clock(clock), .P(P5), .Z(p5_t));
  SinglePulser singlepulser_2 (.Clr(reset), .Clock(clock), .P(P10), .Z(p10_t));
  SinglePulser singlepulser_3 (.Clr(reset), .Clock(clock), .P(P20), .Z(p20_t));
  SinglePulser singlepulser_4 (.Clr(reset), .Clock(clock), .P(Pcoffee), .Z(pCoffee_t));
  SinglePulser singlepulser_5 (.Clr(reset), .Clock(clock), .P(Ptea), .Z(pTea_t));
  SinglePulser singlepulser_6 (.Clr(reset), .Clock(clock), .P(Pchange), .Z(pChange_t));
  SinglePulser singlepulser_7 (.Clr(reset), .Clock(clock), .P(Pnext), .Z(pNext_t));
  Multiplexer #(.Bits(6)) multiplexer_2 (
    .sel(cCoffee), .in_0(multiplexer_1_out), .in_1(ACoffee), .out(multiplexer_2_out));
  Multiplexer #(.Bits(6)) multiplexer_3 (.sel(cTea), .in_0(multiplexer_2_out), .in_1(ATea), .out(multiplexer_3_out));
  Multiplexer multiplexer_4 (.sel(cTea), .in_0(1'b0), .in_1(1'b1), .out(multiplexer_4_out));
  Multiplexer multiplexer_5 (.sel(pReset), .in_0(TeaOut), .in_1(1'b0), .out(multiplexer_5_out));
  Multiplexer multiplexer_6 (.sel(ProductOut), .in_0(multiplexer_4_out), .in_1(multiplexer_5_out), .out(NteaOut));
  D_FF_AS #(.Bits(6)) d_ff_as_1 (.Set(1'b0), .D(Nbalance), .C(clock), .Clr(reset), .Q(Balance));  // open: nQ
  D_FF_AS d_ff_as_2 (.Set(1'b0), .D(NcoffeeOut), .C(clock), .Clr(reset), .Q(CoffeeOut));  // open: nQ
  D_FF_AS d_ff_as_3 (.Set(1'b0), .D(NteaOut), .C(clock), .Clr(reset), .Q(TeaOut));  // open: nQ
  D_FF_AS #(.Bits(2)) d_ff_as_4 (.Set(1'b0), .D(Nchange5), .C(clock), .Clr(reset), .Q(Change5));  // open: nQ
  D_FF_AS #(.Bits(2)) d_ff_as_5 (.Set(1'b0), .D(Nchange10), .C(clock), .Clr(reset), .Q(Change10));  // open: nQ
  D_FF_AS #(.Bits(2)) d_ff_as_6 (.Set(1'b0), .D(Nchange20), .C(clock), .Clr(reset), .Q(Change20));  // open: nQ
  Multiplexer #(.Bits(6)) multiplexer_7 (.sel(c20), .in_0(multiplexer_3_out), .in_1(A20), .out(multiplexer_7_out));
  Multiplexer #(.Bits(6)) multiplexer_8 (.sel(c10), .in_0(multiplexer_7_out), .in_1(A10), .out(multiplexer_8_out));
  Multiplexer #(.Bits(6)) multiplexer_9 (.sel(c5), .in_0(multiplexer_8_out), .in_1(A5), .out(multiplexer_9_out));
  Multiplexer #(.Bits(6)) multiplexer_10 (.sel(pChange_t), .in_0(Balance), .in_1({6{1'b0}}), .out(multiplexer_10_out));
  Multiplexer multiplexer_11 (.sel(cCoffee), .in_0(1'b0), .in_1(1'b1), .out(multiplexer_11_out));
  Multiplexer multiplexer_12 (.sel(pReset), .in_0(CoffeeOut), .in_1(1'b0), .out(multiplexer_12_out));
  Multiplexer #(.Bits(6)) multiplexer_13 (
    .sel(ProductOut), .in_0(multiplexer_9_out), .in_1(multiplexer_10_out), .out(Nbalance));
  Multiplexer multiplexer_14 (.sel(ProductOut), .in_0(multiplexer_11_out), .in_1(multiplexer_12_out), .out(NcoffeeOut));
  or or_1 (ProductOut, CoffeeOut, TeaOut);
  or or_2 (pReset, pChange_t, pNext_t);
  LookUpTable #(.Bits(2)) lookuptable_1 (
    .in0(Balance[0]), .in1(Balance[1]), .in2(Balance[2]), .in3(Balance[3]), .in4(Balance[4]),
    .in5(Balance[5]), .out(lookuptable_1_out));
  LookUpTable #(.Bits(2)) lookuptable_2 (
    .in0(Balance[0]), .in1(Balance[1]), .in2(Balance[2]), .in3(Balance[3]), .in4(Balance[4]),
    .in5(Balance[5]), .out(lookuptable_2_out));
  LookUpTable #(.Bits(2)) lookuptable_3 (
    .in0(Balance[0]), .in1(Balance[1]), .in2(Balance[2]), .in3(Balance[3]), .in4(Balance[4]),
    .in5(Balance[5]), .out(lookuptable_3_out));
  Comparator #(.Bits(6)) comparator_1 (.a(Balance), .b(6'b101101), .gt(M45));  // open: eq, lt
  Comparator #(.Bits(6)) comparator_2 (.a(Balance), .b(6'b101000), .gt(M40));  // open: eq, lt
  Comparator #(.Bits(6)) comparator_3 (.a(Balance), .b(6'b011110), .gt(M30));  // open: eq, lt
  Comparator #(.Bits(6)) comparator_4 (.a(Balance), .b(6'b010011), .gt(M20));  // open: eq, lt
  Comparator #(.Bits(6)) comparator_5 (.a(Balance), .b(6'b011000), .gt(M25));  // open: eq, lt
  and and_1 (c5, p5_t, ~M45);  // And
  and and_2 (c10, p10_t, ~M40);  // And
  and and_3 (c20, p20_t, ~M30);  // And
  and and_4 (cTea, pTea_t, M20);
  and and_5 (cCoffee, pCoffee_t, M25);
  Multiplexer #(.Bits(2)) multiplexer_15 (.sel(pChange_t), .in_0(Change5), .in_1(lookuptable_1_out), .out(Nchange5));
  Multiplexer #(.Bits(2)) multiplexer_16 (.sel(pChange_t), .in_0(Change10), .in_1(lookuptable_2_out), .out(Nchange10));
  Multiplexer #(.Bits(2)) multiplexer_17 (.sel(pChange_t), .in_0(Change20), .in_1(lookuptable_3_out), .out(Nchange20));
  Add #(.Bits(6)) add_1 (.a(Balance), .b(6'b000101), .c_i(1'b0), .s(A5));  // open: c_o
  Add #(.Bits(6)) add_2 (.a(Balance), .b(6'b001010), .c_i(1'b0), .s(A10));  // open: c_o
  Add #(.Bits(6)) add_3 (.a(Balance), .b(6'b010100), .c_i(1'b0), .s(A20));  // open: c_o
  Sub #(.Bits(6)) sub_1 (.a(Balance), .b(6'b011001), .c_i(1'b0), .s(ACoffee));  // open: c_o
  Sub #(.Bits(6)) sub_2 (.a(Balance), .b(6'b010100), .c_i(1'b0), .s(ATea));  // open: c_o

  // Other names for the same wires on the sheet: CLK = clock; CLR = reset

  // Notes on the sheet:
  //   contents of lookuptable_1 (hex, n*v repeats v):
  //   5*0,1,9*0,1,9*0,1,9*0,1,9*0,1
  //   contents of lookuptable_2 (hex, n*v repeats v):
  //   10*0,1,4*0,1,14*0,1,4*0,1,14*0,1
  //   contents of lookuptable_3 (hex, n*v repeats v):
  //   20*0,1,4*0,1,4*0,1,4*0,1,4*0,2,4*0,2,4*0,2
endmodule
