// Digital circuit Template.dig as structural Verilog
module Template (
  input  P5,
  input  reset,
  input  clock,
  input  P10,
  input  P20,
  input  Pcoffee,
  input  Ptea,
  input  Pchange,
  input  Pnext,
  output [5:0] Balance,
  output CoffeeOut,
  output TeaOut,
  output [1:0] Change5,
  output [1:0] Change10,
  output [1:0] Change20
);

  wire _5, _10, _20, change_reset, coffee, comparator_1_gt, comparator_2_gt, comparator_3_lt,
       comparator_4_lt, comparator_5_lt, d_ff_1_q, d_ff_2_q, d_ff_3_nq, d_ff_4_nq, d_ff_5_nq, d_ff_6_nq,
       d_ff_7_q, d_ff_8_q, d_ff_9_q, d_ff_10_q, d_ff_11_q, d_ff_12_q, d_ff_13_q, d_ff_14_q, d_ff_17_nq,
       d_ff_18_nq, d_ff_19_nq, d_ff_20_q, d_ff_21_q, d_ff_22_q, d_ff_23_q, d_ff_24_q, d_ff_25_q, or_1_out,
       Q5, Q10, Q20, Qchange, Qcoffee, Qnext, Qtea, rs_ff_as_1_q, rs_ff_as_2_q, tea;
  wire [1:0] div_1_q, div_2_q, div_3_q, multiplexer_2_out, multiplexer_3_out, multiplexer_4_out;
  wire [5:0] add_1_s, div_1_r, div_2_r, lookuptable_1_out, multiplexer_1_out;
  wire [5:2] div_1_q_2, div_2_q_2, div_3_q_2;

  or or_1 (or_1_out, Qchange, Qnext, reset);
  D_FF d_ff_1 (.D(Pnext), .C(clock), .Q(d_ff_1_q));  // open: nQ
  D_FF d_ff_2 (.D(Pchange), .C(clock), .Q(d_ff_2_q));  // open: nQ
  Comparator #(.Bits(6)) comparator_1 (.a(Balance), .b(6'b011000), .gt(comparator_1_gt));  // open: eq, lt
  Comparator #(.Bits(6)) comparator_2 (.a(Balance), .b(6'b010011), .gt(comparator_2_gt));  // open: eq, lt
  Comparator #(.Bits(6)) comparator_3 (.a(Balance), .b(6'b101110), .lt(comparator_3_lt));  // open: gt, eq
  Comparator #(.Bits(6)) comparator_4 (.a(Balance), .b(6'b101001), .lt(comparator_4_lt));  // open: gt, eq
  Comparator #(.Bits(6)) comparator_5 (.a(Balance), .b(6'b011111), .lt(comparator_5_lt));  // open: gt, eq
  D_FF d_ff_3 (.D(d_ff_1_q), .C(clock), .nQ(d_ff_3_nq));  // open: Q
  D_FF d_ff_4 (.D(d_ff_2_q), .C(clock), .nQ(d_ff_4_nq));  // open: Q
  D_FF d_ff_5 (.D(Ptea), .C(clock), .nQ(d_ff_5_nq));  // open: Q
  D_FF d_ff_6 (.D(Pcoffee), .C(clock), .nQ(d_ff_6_nq));  // open: Q
  and and_1 (coffee, Qcoffee, comparator_1_gt, ~TeaOut, ~CoffeeOut);  // And
  and and_2 (tea, Qtea, comparator_2_gt, ~TeaOut, ~CoffeeOut);  // And
  RS_FF_AS rs_ff_as_1 (.S(tea), .R(or_1_out), .Q(rs_ff_as_1_q));  // open: nQ
  RS_FF_AS rs_ff_as_2 (.S(coffee), .R(or_1_out), .Q(rs_ff_as_2_q));  // open: nQ
  D_FF d_ff_7 (.D(d_ff_1_q), .C(clock), .Q(d_ff_7_q));  // open: nQ
  D_FF d_ff_8 (.D(d_ff_3_nq), .C(clock), .Q(d_ff_8_q));  // open: nQ
  D_FF d_ff_9 (.D(d_ff_2_q), .C(clock), .Q(d_ff_9_q));  // open: nQ
  D_FF d_ff_10 (.D(d_ff_4_nq), .C(clock), .Q(d_ff_10_q));  // open: nQ
  D_FF d_ff_11 (.D(Ptea), .C(clock), .Q(d_ff_11_q));  // open: nQ
  D_FF d_ff_12 (.D(d_ff_5_nq), .C(clock), .Q(d_ff_12_q));  // open: nQ
  D_FF d_ff_13 (.D(Pcoffee), .C(clock), .Q(d_ff_13_q));  // open: nQ
  D_FF d_ff_14 (.D(d_ff_6_nq), .C(clock), .Q(d_ff_14_q));  // open: nQ
  and and_3 (_5, ~TeaOut, ~CoffeeOut, comparator_3_lt, Q5);  // And
  and and_4 (_10, ~TeaOut, ~CoffeeOut, comparator_4_lt, Q10);  // And
  and and_5 (_20, ~TeaOut, ~CoffeeOut, comparator_5_lt, Q20);  // And
  D_FF d_ff_15 (.D(rs_ff_as_1_q), .C(clock), .Q(TeaOut));  // open: nQ
  D_FF d_ff_16 (.D(rs_ff_as_2_q), .C(clock), .Q(CoffeeOut));  // open: nQ
  and and_6 (Qnext, d_ff_7_q, d_ff_8_q);
  and and_7 (Qchange, d_ff_9_q, d_ff_10_q);
  and and_8 (Qtea, d_ff_11_q, d_ff_12_q);
  and and_9 (Qcoffee, d_ff_13_q, d_ff_14_q);
  D_FF d_ff_17 (.D(P5), .C(clock), .nQ(d_ff_17_nq));  // open: Q
  D_FF d_ff_18 (.D(P10), .C(clock), .nQ(d_ff_18_nq));  // open: Q
  D_FF d_ff_19 (.D(P20), .C(clock), .nQ(d_ff_19_nq));  // open: Q
  LookUpTable #(.Bits(6)) lookuptable_1 (
    .in0(_5), .in1(_10), .in2(_20), .in3(tea), .in4(coffee), .out(lookuptable_1_out));
  D_FF d_ff_20 (.D(P5), .C(clock), .Q(d_ff_20_q));  // open: nQ
  D_FF d_ff_21 (.D(d_ff_17_nq), .C(clock), .Q(d_ff_21_q));  // open: nQ
  D_FF d_ff_22 (.D(P10), .C(clock), .Q(d_ff_22_q));  // open: nQ
  D_FF d_ff_23 (.D(d_ff_18_nq), .C(clock), .Q(d_ff_23_q));  // open: nQ
  D_FF d_ff_24 (.D(P20), .C(clock), .Q(d_ff_24_q));  // open: nQ
  D_FF d_ff_25 (.D(d_ff_19_nq), .C(clock), .Q(d_ff_25_q));  // open: nQ
  Div #(.Bits(6)) div_1 (.a(Balance), .b(6'b010100), .q({div_1_q_2, div_1_q}), .r(div_1_r));
  Div #(.Bits(6)) div_2 (.a(div_1_r), .b(6'b001010), .q({div_2_q_2, div_2_q}), .r(div_2_r));
  Div #(.Bits(6)) div_3 (.a(div_2_r), .b(6'b000101), .q({div_3_q_2, div_3_q}));  // open: r
  and and_10 (Q5, d_ff_20_q, d_ff_21_q);
  and and_11 (Q10, d_ff_22_q, d_ff_23_q);
  and and_12 (Q20, d_ff_24_q, d_ff_25_q);
  Add #(.Bits(6)) add_1 (.a(Balance), .b(lookuptable_1_out), .c_i(1'b0), .s(add_1_s));  // open: c_o
  or or_2 (change_reset, Qchange, reset);
  Multiplexer #(.Bits(6)) multiplexer_1 (.sel(change_reset), .in_0(add_1_s), .in_1({6{1'b0}}), .out(multiplexer_1_out));
  Multiplexer #(.Bits(2)) multiplexer_2 (.sel(reset), .in_0(div_1_q), .in_1(2'b00), .out(multiplexer_2_out));
  Multiplexer #(.Bits(2)) multiplexer_3 (.sel(reset), .in_0(div_2_q), .in_1(2'b00), .out(multiplexer_3_out));
  Multiplexer #(.Bits(2)) multiplexer_4 (.sel(reset), .in_0(div_3_q), .in_1(2'b00), .out(multiplexer_4_out));
  D_FF #(.Bits(6)) d_ff_26 (.D(multiplexer_1_out), .C(clock), .Q(Balance));  // open: nQ
  D_FF #(.Bits(2)) d_ff_27 (.D(multiplexer_2_out), .C(change_reset), .Q(Change20));  // open: nQ
  D_FF #(.Bits(2)) d_ff_28 (.D(multiplexer_3_out), .C(change_reset), .Q(Change10));  // open: nQ
  D_FF #(.Bits(2)) d_ff_29 (.D(multiplexer_4_out), .C(change_reset), .Q(Change5));  // open: nQ

  // Other names for the same wires on the sheet: bal[5:0] = Balance; clk = clock

  // Notes on the sheet:
  //   contents of lookuptable_1 (hex, n*v repeats v):
  //   0,5,a,0,14,0,0,0,ffffffffffffffec,7*0,ffffffffffffffe7
endmodule
