// Digital circuit test.dig as structural Verilog
module test (
  input  in_2,
  input  clk,
  output out_1
);

  wire d_ff_1_nq, d_ff_2_q, d_ff_3_q;

  D_FF d_ff_1 (.D(in_2), .C(clk), .nQ(d_ff_1_nq));  // open: Q
  D_FF d_ff_2 (.D(in_2), .C(clk), .Q(d_ff_2_q));  // open: nQ
  D_FF d_ff_3 (.D(d_ff_1_nq), .C(clk), .Q(d_ff_3_q));  // open: nQ
  and and_1 (out_1, d_ff_2_q, d_ff_3_q);

  // Other names for the same wires on the sheet: Clock = clk
endmodule
