// Digital circuit 1.dig as structural Verilog
module _1 (
  input  [2:0] A,
  input  [2:0] B
);

  wire _0, _1, comparator_1_eq, comparator_1_lt, or_2_out;
  wire [2:0] add_1_s;
  wire [3:3] add_1_c_o;

  Add #(.Bits(3)) add_1 (.a(A), .b(B), .c_i(1'b0), .s(add_1_s), .c_o(add_1_c_o[3]));
  Comparator #(.Bits(4)) comparator_1 (
    .a({add_1_c_o[3], add_1_s}), .b(4'b0101), .gt(_1), .eq(comparator_1_eq), .lt(comparator_1_lt));
  or or_1 (_0, comparator_1_eq, comparator_1_lt);
  Seven_Seg seven_seg_1 (.a(_0), .b(or_2_out), .c(or_2_out), .d(_0), .e(_0), .f(_0), .g(1'b0), .dp(1'b0));
  or or_2 (or_2_out, _0, _1);
endmodule
