// Digital circuit 2.dig as structural Verilog
module _2 (
  input  S0,
  input  S1,
  input  S2
);

  wire demultiplexer_1_out_0, demultiplexer_1_out_2, demultiplexer_1_out_4, demultiplexer_1_out_5,
       demultiplexer_1_out_6, demultiplexer_1_out_7, or_1_out, or_2_out;

  Demultiplexer #(.Selector_Bits(3)) demultiplexer_1 (
    .sel({S0, S1, S2}), .in(1'b1), .out_0(demultiplexer_1_out_0), .out_2(demultiplexer_1_out_2),
    .out_4(demultiplexer_1_out_4), .out_5(demultiplexer_1_out_5), .out_6(demultiplexer_1_out_6),
    .out_7(demultiplexer_1_out_7));  // open: out_1, out_3
  or or_1 (or_1_out, demultiplexer_1_out_2, demultiplexer_1_out_4, demultiplexer_1_out_5, demultiplexer_1_out_6);
  or or_2 (or_2_out, demultiplexer_1_out_0, demultiplexer_1_out_2, demultiplexer_1_out_4, demultiplexer_1_out_6, demultiplexer_1_out_7);
  // Probe O1 on or_1_out
  // Probe O2 on or_2_out
endmodule
